# Fritzing sketch ArdI2C (saved by Fritzing 0.9.3b)
breadboards: 1

parts:
  MCU1 = Raspberry Pi Zero W
  Q1 = MOSFET-NCHANNEL [package=to-92]
  Q2 = MOSFET-NCHANNEL [package=to-92]
  U1 = POT [package=pot_alpha_rv16af-20]
  Componente2 = ws2812b [package="smd 2812b"]
  Componente3 = Arduino Pro Mini (5V)

nets:
  N1: MCU1.pin_1, Q1.S, Q2.S
  VDD: MCU1.pin_2, U1.A, Componente2.VDD, Componente3.VCC
  N2: MCU1.pin_3, Q2.D
  N3: MCU1.pin_5, Q1.D
  VSS: MCU1.pin_6, MCU1.pin_39, U1.E, Componente2.VSS, Componente3.GND
  N4: Q1.G, Componente3.A4
  N5: Q2.G, Componente3.A5
  N6: U1.S, Componente3.A0
  N7: Componente2.DIN, Componente3.D3

custom parts:
  Raspberry Pi Zero W: The Raspberry Pi Zero is half the size of a Model A+, with twice the utility. A tiny Raspberry Pi that’s affordable enough for any project! · 1Ghz, Single-core CPU · 512MB RAM · Mini HDMI and USB On-The-Go ports · Micro USB power · HAT-compatible 40-pin header. Jan 2018: In this version schematic has been changed so the pins match the GPIO connector. I.e. the left hand pins are all the pins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
